# Fritzing sketch Rpi-GPIO (saved by Fritzing 0.9.2b)
breadboards: 1

parts:
  Raspberry_Pi1 = Raspberry Pi B+
  LED1 = LED - 5mm [color="Red (633nm)" package="5 mm [THT]"]
  LED2 = LED - 5mm [color="Blue (470nm)" package="5 mm [THT]"]
  LED3 = LED - 5mm [color="Green (560nm)" package="5 mm [THT]"]
  S1 = Pushbutton [package="[THT]"]
  S2 = Pushbutton [package="[THT]"]
  DHT1 = DHT11 Humitidy and Temperature Sensor
  J1 = Piezo Speaker

nets:
  N1: Raspberry_Pi1.GPIO5, DHT1.DATA
  N2: Raspberry_Pi1.GPIO6, S2.Pin_1, S2.Pin_2
  N3: Raspberry_Pi1.GPIO13, S1.Pin_1, S1.Pin_2
  N4: Raspberry_Pi1.GPIO24, LED3.anode
  N5: Raspberry_Pi1.GPIO23, LED2.anode
  N6: Raspberry_Pi1.GPIO18, LED1.anode
  N7: Raspberry_Pi1.GND, LED1.cathode, LED2.cathode, LED3.cathode, S1.Pin_3, S1.Pin_4, S2.Pin_3, S2.Pin_4, J1.pin1
  5V: Raspberry_Pi1.5V, DHT1.VDD

custom parts:
  DHT11 Humitidy and Temperature Sensor: DHT11 Humidity and Temperature Sensor
